// Logisim project display_logisim_simul.circ as structural Verilog: 1 circuit, main circuit main
module main (
  input  DEC_EN,
  input  in_2,
  input  CNT_EN,
  input  U_D,
  input  LOAD
);

  wire n74155_1_pin1, n74155_1_pin3, n74155_1_pin4, n74155_1_pin5, n74155_1_pin6, n74155_1_pin7,
       n74155_1_pin8, n74155_1_pin9, n74155_1_pin10, n74155_1_pin11, n74155_1_pin12, n74155_1_pin13,
       n74155_1_pin16, n74191_1_pin7, n74191_1_pin14, n74191_1_pin16;

  LED led_1 (.in(n74155_1_pin4));
  _74155 #(.VccGndPorts("true")) u_74155_1 (
    .pin1(n74155_1_pin1), .pin2(DEC_EN), .pin3(n74155_1_pin3), .pin4(n74155_1_pin4), .pin5(n74155_1_pin5),
    .pin6(n74155_1_pin6), .pin7(n74155_1_pin7), .pin8(n74155_1_pin8), .pin16(n74155_1_pin16),
    .pin15(n74155_1_pin1), .pin14(DEC_EN), .pin13(n74155_1_pin13), .pin12(n74155_1_pin12),
    .pin11(n74155_1_pin11), .pin10(n74155_1_pin10), .pin9(n74155_1_pin9));
  LED led_2 (.in(n74155_1_pin5));
  LED led_3 (.in(n74155_1_pin6));
  LED led_4 (.in(n74155_1_pin7));
  LED led_5 (.in(n74155_1_pin12));
  LED led_6 (.in(n74155_1_pin11));
  LED led_7 (.in(n74155_1_pin10));
  LED led_8 (.in(n74155_1_pin9));
  _74191 #(.VccGndPorts("true")) u_74191_1 (
    .pin1(n74155_1_pin8), .pin2(n74155_1_pin3), .pin3(n74155_1_pin13), .pin4(CNT_EN), .pin5(U_D),
    .pin6(n74155_1_pin1), .pin7(n74191_1_pin7), .pin8(n74155_1_pin8), .pin16(n74191_1_pin16),
    .pin15(n74155_1_pin8), .pin14(n74191_1_pin14), .pin11(LOAD), .pin10(n74155_1_pin8), .pin9(n74155_1_pin8));  // open: pin13, pin12
  Clock clock_1 (.out(n74191_1_pin14));
  // Digital_Oscilloscope #(.frontlines("falling")) digital_oscilloscope_1: pin names not known; wires that end beside it: n74191_1_pin14, n74155_1_pin1, n74155_1_pin3, n74155_1_pin13, in_2
  // also tied to GND on the sheet: n74155_1_pin8
  // also tied to VCC on the sheet: {n74155_1_pin16, n74191_1_pin16}

  // Notes on the sheet:
  //   7
  //   6
  //   5
  //   1Y3  1Y2  1Y1  1Y0  2Y3  2Y2  2Y1  2Y0
  //   4
  //   3
  //   1
  //   2
  //   0
  //   O/B
  //   CLK
  //   GIVE 0 TO RESET
  //   C
  //   B
  //   A
  //   CLOCK PULSE
endmodule
